# Fritzing sketch circuit (saved by Fritzing 0.9.3b)
breadboards: 1

parts:
  Raspberry_Pi_1 = Raspberry Pi 3 [part_number=RPI-3-V1.2]
  S1 = Pushbutton [package="[THT]"]
  LED1 = LED - 5mm [color="Red (633nm)" package="5 mm [THT]"]
  R1 = Resistor [tolerance=±5% resistance=220 package=THT]
  LED2 = LED - 5mm [color="Yellow (585nm)" package="5 mm [THT]"]
  LED3 = LED - 5mm [color="Green (555nm)" package="5 mm [THT]"]
  R2 = Resistor [tolerance=±5% resistance=220 package=THT]
  R3 = Resistor [tolerance=±5% resistance=220 package=THT]
  R4 = Resistor [tolerance=±5% resistance=10k package=THT]

nets:
  N1: Raspberry_Pi_1.3v3, Raspberry_Pi_1.GIPO17, S1.Pin_3, S1.Pin_4, R3.Pin_1, R4.Pin_1
  N2: Raspberry_Pi_1.GIPO18, R2.Pin_1
  N3: Raspberry_Pi_1.GIPO14, R1.Pin_1
  N4: Raspberry_Pi_1.GND, LED1.cathode, LED2.cathode, LED3.cathode, R4.Pin_0
  N5: S1.Pin_1, S1.Pin_2
  N6: LED1.anode, R3.Pin_0
  N7: R1.Pin_0, LED3.anode
  N8: LED2.anode, R2.Pin_0

notes:
  3v3
  GND
  GPIO17
  GPIO14
  GPIO18
